// Logisim project CocaCola.circ as structural Verilog
module main (
  input  in_1,
  input  in_2,
  input  in_3,
  input  in_4,
  input  in_5,
  output out_6,
  output out_7,
  output out_8,
  output out_9
);

  wire button_1_out;

  Button button_1 (.out(button_1_out));
  COCACOAL cocacoal_1 (
    .clk(button_1_out), .reset(in_1), .F0(in_2), .F1(in_3), .F2(in_4), .F3(in_5), .F4(out_6), .AM(out_7),
    .AT(out_8), .Coke(out_9));
endmodule

// VHDL entity COCACOAL, as the project stores it:
--------------------------------------------------------------------------------
-- Project :
-- File    :
-- Autor   :
-- Date    :
--
--------------------------------------------------------------------------------
-- Description :
--
--------------------------------------------------------------------------------

LIBRARY ieee;
USE ieee.std_logic_1164.all;
use ieee.numeric_std.all;


ENTITY COCACOAL IS
  PORT (
   clk: in std_logic;
    reset: in std_logic;
    F0: in std_logic; -- fotocelula pentru moneda de 5 bani
    F1: in std_logic; -- fotocelula pentru moneda de 10 bani
    F2: in std_logic; -- fotocelula pentru moneda de 50 bani
    F3: in std_logic; -- fotocelula pentru respingere moneda/corpuri straine
    F4: out std_logic; -- semnal de acceptare a monedei
    AM: out std_logic; -- semnal de acceptare a monezilor
    AT: out std_logic; -- semnal de total
    Coke: out std_logic -- semnal de eliberare Coca Cola
    );
END COCACOAL;

--------------------------------------------------------------------------------
--Complete your VHDL description below
--------------------------------------------------------------------------------

ARCHITECTURE TypeArchitecture OF COCACOAL IS

 -- Definim starea sistemului
  type state is (S0, S1, S2, S3);
  signal current_state, next_state: state;

  -- Definim variabilele necesare pentru calcularea totalului si pretului
  signal total: unsigned(7 downto 0) := (others => '0');
  constant price: unsigned(7 downto 0) := "00000001"; -- pretul este de 1 leu sau 100 de bani


BEGIN
  process (clk, reset)
begin
    if reset = '1' then
      current_state <= S0; -- stare initiala
      total <= (others => '0'); -- resetam totalul
      F4 <= '0'; -- resetam semnalul de acceptare a monedei
      AM <= '0'; -- resetam semnalul de acceptare a monezilor
      AT <= '0'; -- resetam semnalul de total
      Coke <= '0'; -- resetam semnalul de eliberare Coca Cola
   
    elsif rising_edge(clk) then
      current_state <= next_state;
    end if;
  end process;

   -- Definim conditiile de tranzitie intre starile sistemului
  process (current_state, F0, F1, F2, F3)
  begin
    case current_state is
    
      when S0 =>
        if F0 = '1' then
          next_state <= S1;
          F4 <= '1'; -- semnal de acceptare a monedei
          total <= total + "00000101"; -- adaugam moneda de 5 bani la total
          
    elsif F1 = '1' then
          next_state <= S1;
          F4 <= '1'; -- semnal de acceptare a monedei
          total <= total + "00001010"; -- adaugam moneda de 10 bani la total
          
    elsif F2 = '1' then
      next_state <= S1;
      F4 <= '1'; -- semnal de acceptare a monedei
      total <= total + "00110010"; -- adaugam moneda de 50 bani la total
      
    elsif F3 = '1' then
      next_state <= S0; -- daca detectam o moneda neacceptata sau corp strain, revenim la starea initiala
      F4 <= '0';
      
    else
      next_state <= S0; -- asteptam sa primim o moneda
      
    end if;
    
  when S1 =>
    if total < price then
      AM <= '1'; -- semnal de acceptare a monezilor
      F4 <= '0'; -- resetam semnalul de acceptare a monedei
      next_state <= S0; -- monedele sunt returnate
    
    else
      AM <= '0'; -- nu mai acceptam monezi
      AT <= '1'; -- semnal de total
      next_state <= S2; -- trecem la starea urmatoare
    end if;
    
  when S2 =>
    Coke <= '1'; -- semnal de eliberare Coca Cola
    next_state <= S3; -- trecem la starea urmatoare
    
  when S3 =>
    Coke <= '0'; -- resetam semnalul de eliberare Coca Cola
    AT <= '0'; -- resetam semnalul de total
    total <= (others => '0'); -- resetam totalul
    next_state <= S0; -- revenim la starea initiala
    
end case;
end process;

END TypeArchitecture;
