// Logisim project OFICIAL_PROIECT.circ as structural Verilog
module main (
  output [8:0] REST,
  output [8:0] SUCURI,
  output [8:0] BANI_INTRODUSI
);

  wire BANI5_out, BANI10_out, BANI50_out, clock_1_out, continue_out, controlunit_1_am, controlunit_1_at,
       controlunit_1_cola, controlunit_1_fs, controlunit_1_os, controlunit_1_rm,
       controlunit_1_soldinsuficient, dispense_out, OBIECT_strain_out;

  Button BANI5 (.out(BANI5_out));
  Button BANI10 (.out(BANI10_out));
  Button BANI50 (.out(BANI50_out));
  Button OBIECT_strain (.out(OBIECT_strain_out));
  Button #(.press("passive")) dispense (.out(dispense_out));
  Button \continue  (.out(continue_out));
  Clock clock_1 (.out(clock_1_out));
  ControlUnit controlunit_1 (
    .Clk(clock_1_out), .F0(BANI5_out), .F1(BANI10_out), .F2(BANI50_out), .F3(OBIECT_strain_out),
    .buton(dispense_out), .continua(continue_out), .RM(controlunit_1_rm), .FS(controlunit_1_fs),
    .AM(controlunit_1_am), .AT(controlunit_1_at), .Cola(controlunit_1_cola),
    .SoldInsuficient(controlunit_1_soldinsuficient), .OS(controlunit_1_os), .restOut(REST),
    .sucuriRamase(SUCURI), .TOTAL(BANI_INTRODUSI));
  LED Returnare_Monede (.in(controlunit_1_rm));
  LED Fara_Cola (.in(controlunit_1_fs));
  LED Accept_Moneda (.in(controlunit_1_am));
  LED Accept_Total (.in(controlunit_1_at));
  LED Coca_Cola (.in(controlunit_1_cola));
  LED Sold_Insuficient (.in(controlunit_1_soldinsuficient));
  LED ObiectStrain (.in(controlunit_1_os));
endmodule

// VHDL entity ControlUnit, as the project stores it:
LIBRARY ieee;
USE ieee.std_logic_1164.all;
use ieee.numeric_std.all;
use ieee.std_logic_unsigned.all;

ENTITY ControlUnit IS
  PORT (
 		Clk: in std_logic;
  		F0,F1,F2,F3, buton, continua: in std_logic;
  		RM,FS,AM,AT,Cola, SoldInsuficient, OS: out std_logic;
  		restOut: out std_logic_vector(8 downto 0);
  		sucuriRamase: out std_logic_vector(8 downto 0);
  		TOTAL: out std_logic_vector(8 downto 0)
  		);
END ControlUnit;

--------------------------------------------------------------------------------
--Complete your VHDL description below
--------------------------------------------------------------------------------

ARCHITECTURE comportamentala OF ControlUnit IS

	
type STATE_T is (idle, decizie, verif_total, IM, continue);
signal STATE, NXSTATE: STATE_T;
signal sucuri: std_logic_vector(8 downto 0) := "000000011";
signal rest: std_logic_vector(8 downto 0) := "000000000";
signal suma: std_logic_vector(8 downto 0) := "000000000";

BEGIN

UPDATE_STATE: process (Clk)
			begin
				if (rising_edge(ClK)) then
					STATE <= NXSTATE;
					end if;
			end process UPDATE_STATE;
			

TRANSITIONS: process (STATE,  buton, continua)--POATE SI IM
			begin
				case STATE is
					when idle => if sucuri="000000000" then FS<='1'; NXSTATE<=idle; 
					
								else NXSTATE <= decizie; FS <= '0';
								end if;
								
					when decizie => if buton='0' then NXSTATE <= verif_total;
							   else NXSTATE <= IM;
							   end if;

					when IM => NXSTATE <= decizie;
					
					when verif_total => NXSTATE <= continue;

					when continue => if continua = '1' then NXSTATE <= idle;
					else NXSTATE <= continue;
					end if;
							  		 
				end case;
			end process;

					
Outputs: process (STATE, buton)
		begin
		-- initialization
		case STATE is
					when idle => if(sucuri = "000000000") then FS<= '1';RM<='0';AM<='0';AT<='0';Cola<='0'; SoldInsuficient<='0'; OS<='0';
					else RM<='0';FS<='0';AM<='0';AT<='0';Cola<='0'; SoldInsuficient<='0'; OS<='0'; rest <= "000000000";
						end if;

					when decizie => null;
					
					when verif_total => if suma > "001100100" then rest<="000000000"; AT <='1'; Cola <= '1'; RM <= '1';  rest <= suma - "001100100";sucuri <= sucuri - 1; 
								elsif (suma = "001100100") then rest <="000000000"; AT <= '1'; Cola <= '1'; rest <= suma - "001100100"; sucuri <= sucuri - 1; 
								elsif(suma = "000000000") then RM <= '0'; SoldInsuficient <= '1';
								elsif(suma < "001100100") then  rest <=suma; RM <= '1'; SoldInsuficient<='1'; 
								end if;
								suma <= "000000000"; 
												
					when continue => null;		
					when IM => AM <= '0'; OS<= '0';
						if F0 = '1' then AM <='1'; suma <= suma + "000000101";
						   elsif F1 = '1' then AM <='1'; suma <= suma + "000001010";
						   elsif F2 = '1' then AM <='1'; suma <= suma + "000110010";
						   elsif F3 = '1' then OS <= '1';
						   end if;
				end case;	

				TOTAL <= suma;
				sucuriRamase <= sucuri;
				restOut <= rest;
		end process;	


END comportamentala;

----------------------------------------------------------------------------

library IEEE;
use IEEE.STD_LOGIC_1164.ALL;
use ieee.numeric_std.all;
use ieee.std_logic_unsigned.all;

ENTITY sumator IS
  PORT (
  	a: IN std_logic_vector(8 DOWNTO 0);
  	b: IN std_logic_vector(8 DOWNTO 0);
  	sumaOut: out std_logic_vector(8 downto 0)
    );
END sumator;

ARCHITECTURE TypeArchitecture OF sumator IS

  begin

  sumaOut <= a + b;


END TypeArchitecture;

--------------------------------------------------------------------------------------------------------------
library IEEE;
use IEEE.STD_LOGIC_1164.ALL;
use ieee.numeric_std.all;
use ieee.std_logic_unsigned.all;

ENTITY scazator IS
  PORT (
  	a: IN std_logic_vector(8 DOWNTO 0);
  	aOUT: out std_logic_vector(8 downto 0)
    );
END scazator;

ARCHITECTURE TypeArchitecture OF scazator IS

  begin

  aOUT <= a - 1;


END TypeArchitecture;

// VHDL entity sumator, as the project stores it:
library IEEE;
use IEEE.STD_LOGIC_1164.ALL;
use ieee.numeric_std.all;
use ieee.std_logic_unsigned.all;

ENTITY sumator IS
  PORT (
  	a: IN std_logic_vector(8 DOWNTO 0);
  	b: IN std_logic_vector(8 DOWNTO 0);
  	sumaOut: out std_logic_vector(8 downto 0)
    );
END sumator;

ARCHITECTURE TypeArchitecture OF sumator IS

  begin

  sumaOut <= a + b;

  end TypeArchitecture;

// VHDL entity scazator, as the project stores it:
library IEEE;
use IEEE.STD_LOGIC_1164.ALL;
use ieee.numeric_std.all;
use ieee.std_logic_unsigned.all;

ENTITY scazator IS
  PORT (
  	a: IN std_logic_vector(8 DOWNTO 0);
  	aOUT: out std_logic_vector(8 downto 0)
    );
END scazator;

ARCHITECTURE TypeArchitecture OF scazator IS

  begin

  aOUT <= a - 1;


END TypeArchitecture;
