// Logisim project VendingMachine.circ as structural Verilog
module main (
  input  in_1,
  output out_2,
  output out_3,
  output [8:0] out_4,
  output out_5,
  output [8:0] out_6,
  output out_7,
  output out_8,
  output out_9,
  output [8:0] out_10,
  output [8:0] out_11,
  output [8:0] out_12
);

  wire button_1_out, button_2_out, button_3_out, button_4_out, clock_1_out;
  wire [8:0] controlunit_1_am, undriven;

  Clock clock_1 (.out(clock_1_out));
  Button button_1 (.out(button_1_out));
  Button button_2 (.out(button_2_out));
  Button button_3 (.out(button_3_out));
  Button button_4 (.out(button_4_out));
  ControlUnit controlunit_1 (
    .Clk(clock_1_out), .F0(button_1_out), .F1(in_1), .F2(button_2_out), .F3(button_3_out),
    .buton(button_4_out), .sumaINIT(undriven), .RM(out_2), .FS(out_3), .AT(out_5), .Cola(out_7),
    .SoldInsuficient(out_8), .OS(out_9), .AM(controlunit_1_am), .restOut(out_10), .sucuriRamase(out_11),
    .TOTAL(out_12));
  SelfCascadingAdder selfcascadingadder_1 (.clk(clock_1_out), .A(controlunit_1_am), .totalOut(out_4), .TOTAL(out_6));
endmodule

// VHDL entity ControlUnit, as the project stores it:
LIBRARY ieee;
USE ieee.std_logic_1164.all;
use ieee.numeric_std.all;
use ieee.std_logic_unsigned.all;

ENTITY ControlUnit IS
  PORT (
 		Clk: in std_logic;
  		F0,F1,F2,F3, buton: in std_logic;
  		sumaINIT: in std_logic_vector (8 downto 0);
  		RM,FS,AT,Cola, SoldInsuficient, OS: out std_logic;
  		AM: out std_logic_vector(8 downto 0);
  		restOut: out std_logic_vector(8 downto 0);
  		sucuriRamase: out std_logic_vector(8 downto 0);
  		TOTAL: out std_logic_vector(8 downto 0)
  		);
END ControlUnit;

--------------------------------------------------------------------------------
--Complete your VHDL description below
--------------------------------------------------------------------------------

ARCHITECTURE comportamentala OF ControlUnit IS

	
type STATE_T is (idle, decizie, verif_total, IM);
signal STATE, NXSTATE: STATE_T;
signal sucuri: std_logic_vector(8 downto 0) := "000000111";
signal rest: std_logic_vector(8 downto 0) := "000000000";
signal suma: std_logic_vector(8 downto 0) := "000000000";

BEGIN

UPDATE_STATE: process (Clk)
			begin
				if (rising_edge(ClK)) then
					STATE <= NXSTATE;
					end if;
			end process UPDATE_STATE;
			

TRANSITIONS: process (STATE,  buton)--POATE SI IM
			begin
				case STATE is
					when idle => if sucuri="000000000" then FS<='1'; NXSTATE<=idle; 
					
								else NXSTATE <= decizie; FS <= '0';
								end if;
								
					when decizie => if buton='1' then NXSTATE <= verif_total;
							   else NXSTATE <= IM;
							   end if;

					when verif_total => NXSTATE <= idle;
							   
					when IM => NXSTATE <= decizie;
								 
				end case;
			end process;

					
Outputs: process (STATE, buton)
		begin
		-- initialization
		RM<='0';FS<='0';AT<='0';Cola<='0'; SoldInsuficient<='0'; OS<='0';
		
		case STATE is
					when idle => if(sucuri = "000000000") then FS<= '1';
						end if;

					when decizie => null;
					
					when verif_total => if suma > "001100100" then rest<="000000000"; AT <='1'; Cola <= '1'; RM <= '1';  rest <= suma - "001100100";sucuri <= sucuri - 1;  
								elsif (suma = "001100100") then rest <="000000000"; AT <= '1'; Cola <= '1'; rest <= suma - "001100100"; sucuri <= sucuri - 1;   
								elsif(suma < "001100100") then rest <="000000000"; RM <= '1'; SoldInsuficient<='1';
								end if;
												
								
					when IM => if F0 = '1' then AM <="000000101";
						   elsif F1 = '1' then AM <="000001010"; 
						   elsif F2 = '1' then AM <="000110010"; 
						   elsif F3 = '1' then OS <= '1';
						   end if;
				end case;	
				
				TOTAL <= suma;
				sucuriRamase <= sucuri;
				restOut <= rest;
		end process;	


END comportamentala;



library IEEE;
use IEEE.STD_LOGIC_1164.ALL;
use ieee.numeric_std.all;
use ieee.std_logic_unsigned.all;

ENTITY sumator IS
  PORT (
  	clk: in std_logic;
  	a: IN std_logic_vector(8 DOWNTO 0);
  	b: IN std_logic_vector(8 DOWNTO 0);
  	sumaOut: out std_logic_vector(8 downto 0)
    );
END sumator;

ARCHITECTURE TypeArchitecture OF sumator IS

 begin
  
	process(clk)
	begin 
if(rising_edge(clk)) then
  sumaOut <= a + b;
  end if;

  end process;


END TypeArchitecture;

// VHDL entity SelfCascadingAdder, as the project stores it:
LIBRARY ieee;
USE ieee.std_logic_1164.all;
use ieee.numeric_std.all;
use ieee.std_logic_unsigned.all;

entity SelfCascadingAdder is
    port (
     clk: in std_logic;
        A : in std_logic_vector(8 downto 0);
        totalOut: out std_logic_vector(8 downto 0);
        TOTAL : out std_logic_vector(8 downto 0)
    );
end entity SelfCascadingAdder;


architecture behavioral of SelfCascadingAdder is

component sumator is 
	  port (
     clk: in std_logic;
        A : in std_logic_vector(8 downto 0);
        B : in std_logic_vector(8 downto 0);
        TOTAL : out std_logic_vector(8 downto 0)
    );
   end component;

   signal  A1, B1, totalOut1, TOTAL1: std_logic_vector(8 downto 0);
   signal clk1: std_logic;
   
begin
	process(clk)
	begin
	U1: sumator port map(clk, A, "000000000", TOTAL1);
	U2: sumator port map(clk, A, TOTAL1, TOTAL);

end architecture behavioral;


LIBRARY ieee;
USE ieee.std_logic_1164.all;
use ieee.numeric_std.all;
use ieee.std_logic_unsigned.all;

entity sumator is

	  port (
     clk: in std_logic;
        A : in std_logic_vector(8 downto 0);
        B : in std_logic_vector(8 downto 0);
        TOTAL : out std_logic_vector(8 downto 0)
    );

    end sumator;

architecture porting of sumator is

begin
	TOTAL <= A+B;
end porting;

// VHDL entity memorieRAM, as the project stores it:
--------------------------------------------------------------------------------
-- Project :
-- File    :
-- Autor   :
-- Date    :
--
--------------------------------------------------------------------------------
-- Description :
--
--------------------------------------------------------------------------------

LIBRARY ieee;
USE ieee.std_logic_1164.all;

ENTITY memorieRAM IS
  PORT (
  ------------------------------------------------------------------------------
  --Insert input ports below
    clock      : IN  std_logic;                    -- input bit example
    val        : IN  std_logic_vector(3 DOWNTO 0); -- input vector example
  ------------------------------------------------------------------------------
  --Insert output ports below
    max        : OUT std_logic;                    -- output bit example
    cpt        : OUT std_logic_vector(3 DOWNTO 0)  -- output vector example
    );
END memorieRAM;

--------------------------------------------------------------------------------
--Complete your VHDL description below
--------------------------------------------------------------------------------

ARCHITECTURE TypeArchitecture OF memorieRAM IS

BEGIN


END TypeArchitecture;

// VHDL entity testCOLA, as the project stores it:
LIBRARY ieee;
USE ieee.std_logic_1164.all;
use ieee.numeric_std.all;
use ieee.std_logic_unsigned.all;

ENTITY ControlUnit IS
  PORT (
 		Clk: in std_logic;
  		F0,F1,F2,F3, buton: in std_logic;
  		RM,FS,AM,AT,Cola, SoldInsuficient, OS: out std_logic;
  		restOut: out std_logic_vector(8 downto 0);
  		sucuriRamase: out std_logic_vector(8 downto 0);
  		TOTAL: out std_logic_vector(8 downto 0)
  		);
END ControlUnit;

--------------------------------------------------------------------------------
--Complete your VHDL description below
--------------------------------------------------------------------------------

ARCHITECTURE comportamentala OF ControlUnit IS

	
type STATE_T is (idle, decizie, verif_total, IM);
signal STATE, NXSTATE: STATE_T;
signal sucuri: std_logic_vector(8 downto 0) := "000000000";
signal rest: std_logic_vector(8 downto 0) := "000000000";
signal suma: std_logic_vector(8 downto 0) := "000000000";

BEGIN

UPDATE_STATE: process (Clk)
			begin
				if (rising_edge(ClK)) then
					STATE <= NXSTATE;
					end if;
			end process UPDATE_STATE;
			

TRANSITIONS: process (STATE,  buton)--POATE SI IM
			begin
				case STATE is
					when idle => if sucuri="000000000" then FS<='1'; NXSTATE<=idle; 
					
								else NXSTATE <= decizie; FS <= '0';
								end if;
								
					when decizie => if buton='1' then NXSTATE <= verif_total;
							   else NXSTATE <= IM;
							   end if;

					when verif_total => NXSTATE <= idle;
							   
					when IM => NXSTATE <= decizie;
								 
				end case;
			end process;

					
Outputs: process (STATE, buton)
		begin
		-- initialization
		RM<='0';FS<='0';AM<='0';AT<='0';Cola<='0'; SoldInsuficient<='0'; OS<='0';
		
		case STATE is
					when idle => if(sucuri = "000000000") then FS<= '1';
						end if;

					when decizie => null;
					
					when verif_total => if suma > "001100100" then rest<="000000000"; AT <='1'; Cola <= '1'; RM <= '1';  rest <= suma - "001100100";sucuri <= sucuri - 1; suma <= "000000000"; 
								elsif (suma = "001100100") then rest <="000000000"; AT <= '1'; Cola <= '1'; rest <= suma - "001100100"; sucuri <= sucuri - 1; suma <= "000000000";  
								elsif(suma < "001100100") then rest <="000000000"; RM <= '1'; SoldInsuficient<='1'; suma <= "000000000";
								end if;
												
								
					when IM => if F0 = '1' then AM <='1'; suma <= suma + "000000101";
						   elsif F1 = '1' then AM <='1'; suma <= suma + "000001010";
						   elsif F2 = '1' then AM <='1'; suma <= suma + "000110010";
						   elsif F3 = '1' then OS <= '1';
						   end if;
				end case;	

				TOTAL <= suma;
				sucuriRamase <= sucuri;
				restOut <= rest;
		end process;	


END comportamentala;



library IEEE;
use IEEE.STD_LOGIC_1164.ALL;
use ieee.numeric_std.all;
use ieee.std_logic_unsigned.all;

ENTITY sumator IS
  PORT (
  	a: IN std_logic_vector(8 DOWNTO 0);
  	b: IN std_logic_vector(8 DOWNTO 0);
  	sumaOut: out std_logic_vector(8 downto 0)
    );
END sumator;

ARCHITECTURE TypeArchitecture OF sumator IS

  begin

  sumaOut <= a + b;


END TypeArchitecture;
